// Logisim project ALU.circ as structural Verilog: 1 circuit, main circuit main
module main (
  input  As,
  input  A1,
  input  A0,
  input  Bs,
  input  B1,
  input  B0,
  input  in_7,
  input  in_8,
  output ZF,
  output EF,
  output OF,
  output DZF
);

  wire and_1_out, main_1_s0, main_1_s1, main_1_s2, main_1_ss, main_2_r0, main_2_r1, main_2_r2, main_2_r3,
       main_2_sign, main_3_dzf, main_3_r0, main_3_r1, main_3_sign, multiplexer_2_out, multiplexer_3_out,
       multiplexer_4_out, multiplexer_5_out, n7_segment_display_driver_1_p5, n7_segment_display_driver_1_p6,
       n7_segment_display_driver_1_p7, n7_segment_display_driver_1_p8, n7_segment_display_driver_1_p9,
       n7_segment_display_driver_1_p10, n7_segment_display_driver_1_p11, not_1_out, or_1_out, or_2_out,
       or_3_out;

  add_sub_optimized_main main_1 (
    .Bs(As), .M(in_8), .As(Bs), .B1(A1), .B(A0), .A1(B1), .A(B0), .Ss(main_1_ss), .S2(main_1_s2),
    .S1(main_1_s1), .S0(main_1_s0));
  Multiplication_Final_main main_2 (
    .R0(main_2_r0), .R1(main_2_r1), .R2(main_2_r2), .R3(main_2_r3), .sign(main_2_sign), .A2(As), .A1(A1),
    .A0(A0), .B2(Bs), .B1(B1), .B0(B0));
  rem_main main_3 (
    .R0(main_3_r0), .R1(main_3_r1), .sign(main_3_sign), .DZF(main_3_dzf), .A2(As), .A1(A1), .A0(A0), .B2(Bs),
    .B1(B1), .B0(B0));
  Multiplexer #(.select(2), .enable("false")) multiplexer_1 (
    .in0(main_1_s0), .in1(main_1_s0), .in2(main_2_r0), .in3(main_3_r0), .out(OF), .sel({in_7, in_8}));
  Multiplexer #(.select(2), .enable("false")) multiplexer_2 (
    .in0(main_1_s1), .in1(main_1_s1), .in2(main_2_r1), .in3(main_3_r1), .out(multiplexer_2_out),
    .sel({in_7, in_8}));
  Multiplexer #(.select(2), .enable("false")) multiplexer_3 (
    .in0(main_1_s2), .in1(main_1_s2), .in2(main_2_r2), .in3(1'b0), .out(multiplexer_3_out), .sel({in_7, in_8}));
  Multiplexer #(.select(2), .enable("false")) multiplexer_4 (
    .in0(1'b0), .in1(1'b0), .in2(main_2_r3), .in3(1'b0), .out(multiplexer_4_out), .sel({in_7, in_8}));
  Multiplexer #(.select(2), .enable("false")) multiplexer_5 (
    .in0(main_1_ss), .in1(main_1_ss), .in2(main_2_sign), .in3(main_3_sign), .out(multiplexer_5_out),
    .sel({in_7, in_8}));
  Multiplexer #(.select(2), .enable("false")) multiplexer_6 (
    .in0(1'b0), .in1(1'b0), .in2(1'b0), .in3(main_3_dzf), .out(DZF), .sel({in_7, in_8}));
  or or_1 (or_1_out, multiplexer_4_out, multiplexer_3_out);
  or or_2 (or_2_out, multiplexer_2_out, OF);
  // _7_segment_display_driver 7_segment_display_driver_1: pin names not known; wires that end beside it: multiplexer_4_out, multiplexer_3_out, multiplexer_2_out, OF, n7_segment_display_driver_1_p5, n7_segment_display_driver_1_p6, n7_segment_display_driver_1_p7, n7_segment_display_driver_1_p8, n7_segment_display_driver_1_p9, n7_segment_display_driver_1_p10, n7_segment_display_driver_1_p11
  or or_3 (or_3_out, or_1_out, or_2_out);
  not not_1 (not_1_out, or_3_out);
  _7_Segment_Display u_7_segment_display_1 (.g(and_1_out));  // open: f, a, b, e, d, c, dp
  and and_1 (and_1_out, or_3_out, multiplexer_5_out);
  xor xor_1 (ZF, not_1_out, DZF);
  not not_2 (EF, OF);
  _7_Segment_Display u_7_segment_display_2 (
    .g(n7_segment_display_driver_1_p11), .f(n7_segment_display_driver_1_p10),
    .a(n7_segment_display_driver_1_p5), .b(n7_segment_display_driver_1_p6),
    .e(n7_segment_display_driver_1_p9), .d(n7_segment_display_driver_1_p8), .c(n7_segment_display_driver_1_p7));  // open: dp

  // Notes on the sheet:
  //   As
  //   As
  //   B1
  //   Bs
  //   A1
  //   Bs
  //   B1
  //   A1
  //   A0
  //   B0
  //   A0
  //   B0
  //   R0, R1, R2, R3, Rs, DZF
endmodule
