// Logisim project Multiplication_Final.circ as structural Verilog: 1 circuit, main circuit main
module main (
  input  A2,
  input  A1,
  input  A0,
  input  B2,
  input  B1,
  input  B0,
  output R0,
  output R1,
  output R2,
  output R3,
  output sign
);

  wire and_2_out, and_3_out, and_4_out, and_5_out;

  and and_1 (R0, A0, B0);
  and and_2 (and_2_out, A0, B1);
  and and_3 (and_3_out, A1, B0);
  and and_4 (and_4_out, A1, B1);
  xor xor_1 (R1, and_2_out, and_3_out);
  and and_5 (and_5_out, and_2_out, and_3_out);
  and and_6 (R3, and_5_out, and_4_out);
  xor xor_2 (sign, B2, A2);
  xor xor_3 (R2, and_5_out, and_4_out);
endmodule
