// Logisim project add_sub_2s.circ as structural Verilog
module main (
  input  Bs,
  input  M,
  input  As,
  input  B1,
  input  B,
  input  A1,
  input  A,
  output Ss,
  output S2,
  output S1,
  output S0
);

  wire and_1_out, and_2_out, main_1_p11, main_1_p12, nor_1_out, nor_2_out, not_1_out, not_2_out, not_3_out,
       xor_1_out, xor_2_out, xor_3_out, xor_4_out, xor_5_out, xor_6_out, xor_7_out, y_out;

  not y (y_out, Bs);
  xor xor_1 (xor_1_out, As, M);
  and and_1 (and_1_out, xor_1_out, y_out);
  nor nor_1 (nor_1_out, xor_1_out, y_out);
  not not_1 (not_1_out, xor_1_out);
  nor nor_2 (nor_2_out, and_1_out, nor_1_out);
  and and_2 (and_2_out, not_1_out, y_out);
  xor xor_2 (xor_2_out, A, and_1_out);
  xor xor_3 (xor_3_out, A1, and_1_out);
  xor xor_4 (xor_4_out, B, nor_1_out);
  xor xor_5 (xor_5_out, B1, nor_1_out);
  not not_2 (not_2_out, nor_2_out);
  xor xor_6 (xor_6_out, main_1_p11, Ss);
  xor xor_7 (xor_7_out, main_1_p12, Ss);
  // _4_bit_full_adder_new_main main_1: pin names not known; wires that end beside it: xor_2_out, xor_4_out, xor_3_out, xor_5_out, xor_6_out, Ss, xor_7_out, 1'b0, Ss, S2, main_1_p11, main_1_p12, S0, S1
  not not_3 (not_3_out, S0);
  and comp_and_carry (Ss, not_3_out, not_2_out);
  // NOR_Gate nor_3 has open pins: in0=Ss, in1=and_2_out, out=open
endmodule
