// Logisim project add_sub_optimized.circ as structural Verilog
module main (
  input  Bs,
  input  M,
  input  As,
  input  B1,
  input  B,
  input  A1,
  input  A,
  output Ss,
  output S2,
  output S1,
  output S0
);

  wire and_1_out, and_2_out, comp_and_carry_out, main_1_p7, main_1_p8, main_1_p9, main_2_p7, main_2_p8,
       main_2_p9, nor_1_out, nor_2_out, nor_4_out, not_1_out, not_2_out, not_3_out, xor_1_out, xor_2_out,
       xor_3_out, xor_4_out, xor_5_out, y_out;

  not y (y_out, Bs);
  xor xor_1 (xor_1_out, As, M);
  and and_1 (and_1_out, xor_1_out, y_out);
  nor nor_1 (nor_1_out, xor_1_out, y_out);
  not not_1 (not_1_out, xor_1_out);
  nor nor_2 (nor_2_out, and_1_out, nor_1_out);
  and and_2 (and_2_out, not_1_out, y_out);
  xor xor_2 (xor_2_out, A, and_1_out);
  xor xor_3 (xor_3_out, A1, and_1_out);
  xor xor_4 (xor_4_out, B, nor_1_out);
  xor xor_5 (xor_5_out, B1, nor_1_out);
  not not_2 (not_2_out, nor_2_out);
  // _4_bit_full_adder_new_main main_1: pin names not known; wires that end beside it: xor_2_out, xor_4_out, xor_3_out, xor_5_out, 1'b0, 1'b0, main_1_p7, main_1_p8, main_1_p9
  and comp_and_carry (comp_and_carry_out, main_1_p9, not_2_out);
  // _4_bit_full_adder_new_main main_2: pin names not known; wires that end beside it: comp_and_carry_out, main_1_p7, main_1_p8, 1'b0, main_1_p9, 1'b0, main_2_p7, main_2_p8, main_2_p9
  not not_3 (not_3_out, comp_and_carry_out);
  nor nor_3 (Ss, comp_and_carry_out, and_2_out);
  nor nor_4 (nor_4_out, main_1_p9, nor_2_out);
  and and_3 (S2, main_2_p9, not_3_out);
  xor xor_6 (S0, main_2_p7, nor_4_out);
  xor xor_7 (S1, main_2_p8, nor_4_out);
endmodule
