// Logisim project rem.circ as structural Verilog: 1 circuit, main circuit main
module main (
  input  A2,
  input  A1,
  input  A0,
  input  B2,
  input  B1,
  input  B0,
  output R0,
  output R1,
  output sign,
  output DZF
);

  wire and_1_out, and_2_out, and_3_out, and_4_out, not_1_out, not_2_out;

  not not_1 (not_1_out, A0);
  and and_1 (and_1_out, A0, B1);
  and and_2 (and_2_out, A1, B0);
  and and_3 (and_3_out, A1, B1);
  and and_4 (and_4_out, not_1_out, B0);
  nor nor_1 (DZF, B0, B1);
  not not_2 (not_2_out, and_2_out);
  and and_5 (R1, and_3_out, and_4_out);
  and and_6 (R0, and_1_out, not_2_out);

  assign sign = A2;
endmodule
